# Fritzing sketch ResistanceLights (saved by Fritzing 0.9.8b)
breadboards: 1

parts:
  Part1 = Arduino Uno (Rev3) - ICSP
  R1 = Resistor [tolerance=±5% resistance=220 package="1206 [SMD]"]
  R3 = Resistor [tolerance=±5% resistance=220 package="1206 [SMD]"]
  R4 = Resistor [tolerance=±5% resistance=220 package="1206 [SMD]"]
  R5 = Resistor [tolerance=±5% resistance=220 package="1206 [SMD]"]
  R6 = Resistor [tolerance=±5% resistance=220 package="1206 [SMD]"]
  LED1 = LED - 5mm [color="Blue (525nm)" current=0.030 package="5 mm [THT]"]
  LED2 = LED - 5mm [color="Green (570nm)" current=0.030 package="5 mm [THT]"]
  LED3 = LED - 5mm [color="Yellow (595nm)" current=0.030 package="5 mm [THT]"]
  LED4 = LED - 5mm [color="Orange (620nm)" current=0.030 package="5 mm [THT]"]
  LED5 = LED - 5mm [color="Red (633nm)" current=0.030 package="5 mm [THT]"]
  R7 = TRIMPOT [package=3362u-2]

nets:
  N1: Part1.GND, LED1.cathode, LED3.cathode, LED4.cathode, LED5.cathode, R7.CCW
  N2: Part1.D2, R1.Pin_1
  N3: Part1.D3_PWM, R3.Pin_1
  N4: Part1.D4, R4.Pin_1
  N5: Part1.D5_PWM, R5.Pin_1
  N6: Part1.D7, R6.Pin_1
  N7: Part1.5V, R7.CW
  N8: R1.Pin_0, LED1.anode
  N9: R3.Pin_0, LED2.anode
  N10: R4.Pin_0, LED3.anode
  N11: R5.Pin_0, LED4.anode
  N12: R6.Pin_0, LED5.anode
