# Fritzing sketch TrafficLightCircuit (saved by Fritzing 0.9.8b)
breadboards: 1

parts:
  Part1 = Arduino Uno (Rev3) - ICSP
  LED1 = LED - 5mm [color="Red (633nm)" current=0.030 package="5 mm [THT]"]
  LED2 = LED - 5mm [color="Yellow (595nm)" current=0.030 package="5 mm [THT]"]
  LED3 = LED - 5mm [color="Green (570nm)" current=0.030 package="5 mm [THT]"]
  R1 = Resistor [tolerance=±5% resistance=220 package="1206 [SMD]"]
  R2 = Resistor [tolerance=±5% resistance=220 package="1206 [SMD]"]
  R3 = Resistor [tolerance=±5% resistance=220 package="1206 [SMD]"]
  R4 = Resistor [tolerance=±5% resistance=220 package="1206 [SMD]"]
  R5 = Resistor [tolerance=±5% resistance=220 package="1206 [SMD]"]
  R6 = Resistor [tolerance=±5% resistance=220 package="1206 [SMD]"]
  LED7 = LED - 5mm [color="Red (633nm)" current=0.030 package="5 mm [THT]"]
  LED8 = LED - 5mm [color="Green (570nm)" current=0.030 package="5 mm [THT]"]
  LED9 = LED - 5mm [color="Yellow (595nm)" current=0.030 package="5 mm [THT]"]

nets:
  N1: Part1.D8, R4.Pin_1
  N2: Part1.D10_PWM/SS, R6.Pin_1
  N3: Part1.D1/TX, R2.Pin_1
  N4: Part1.D2, R3.Pin_1
  N5: Part1.D3_PWM, R1.Pin_1
  N6: Part1.GND, LED1.cathode, LED2.cathode, LED3.cathode, LED7.cathode, LED8.cathode, LED9.cathode
  N7: LED1.anode, R1.Pin_0
  N8: LED2.anode, R3.Pin_0
  N9: LED3.anode, R2.Pin_0
  N10: R4.Pin_0, LED8.anode
  N11: R5.Pin_0, LED9.anode
  N12: R6.Pin_0, LED7.anode
